// Logisim project alu-control.circ as structural Verilog: 1 circuit, main circuit main
module main (
  input  [1:0] Opcode,
  input  [5:0] Funct,
  input  [1:0] sh,
  output [3:0] ALUControl
);

  wire comparator_1_eq;
  wire [1:0] multiplexer_2_out;
  wire [3:0] multiplexer_1_out, multiplexer_3_out;

  Multiplexer #(.select(2), .width(4)) multiplexer_1 (
    .in0(4'b0100), .in1(4'b0101), .in2(4'b0110), .out(multiplexer_1_out), .sel(sh), .en(1'b1));  // open: in3
  Multiplexer #(.select(2), .width(2), .enable("false")) multiplexer_2 (
    .in0(2'b00), .in1(2'b01), .in2(2'b10), .out(multiplexer_2_out), .sel(Opcode));  // open: in3
  Multiplexer #(.select(4), .width(4)) multiplexer_3 (
    .in0(4'b0000), .in1(4'b0010), .in2(4'b1000), .in4(4'b0111), .in10(4'b1000), .in12(4'b0001),
    .in13(4'b1101), .in15(4'b0011), .out(multiplexer_3_out), .sel(Funct[4:1]), .en(comparator_1_eq));  // open: in3, in5, in6, in7, in8, in9, in11, in14
  Comparator #(.width(2)) comparator_1 (.a(multiplexer_2_out), .b(2'b00), .eq(comparator_1_eq));  // open: gt, lt
  Multiplexer #(.select(2), .width(4), .enable("false")) multiplexer_4 (
    .in0(multiplexer_3_out), .out(ALUControl), .sel(Opcode));  // open: in1, in2, in3

  // Other names for the same wires on the sheet: Ctrl[3:0] = ALUControl; FN[5:0] = Funct; OP[1:0] = Opcode

  // Notes on the sheet:
  //   shifts instruction
  //   DO NOT MOVE, CHANGE, ADD, OR REMOVE INPUTS AND OUTPUTS!!!
  //   data-processing Instruction
endmodule
